# Fritzing sketch SecurityNode (saved by Fritzing 0.7.0b)
stripboards: 1

parts:
  J2 = screw terminal, 8 pins
  J3 = male pin header, 6 pins [form="♂ (male)"]
  J4 = male pin header, 6 pins [form="♂ (male)"]
  J5 = male pin header, 6 pins [form="♂ (male)"]
  J6 = male pin header, 6 pins [form="♂ (male)"]
  Part1 = JeeNode wireless microcontroller  # not connected
  U1 = Voltage Regulator - 5V [part_number=7805 package="TO220 [THT]"]
  R1 = Resistor [tolerance=±5% resistance=1k package=THT]
  R2 = Resistor [tolerance=±5% resistance=1k package=THT]
  Q2 = NPN-Transistor [part_number=2N3704 package="TO92 [THT]"]
  Q3 = NPN-Transistor [part_number=2N3704 package="TO92 [THT]"]
  J1 = screw terminal, 8 pins
  C2 = Ceramic Capacitor [capacitance=0.1µF voltage=35V package="100 mil [THT, multilayer]"]
  C3 = Ceramic Capacitor [capacitance=0.1µF voltage=35V package="100 mil [THT, multilayer]"]
  S1 = Toggle Switch [package=THT]
  T1 = TMP36 Temperature Sensor [package="TO92 [THT]"]

nets:
  12V: J2.pin1, U1.input_voltage, J1.pin4, J1.pin8, C3.1
  GND: J2.pin2, J2.pin3, J2.pin5, J2.pin7, J3.pin4, U1.GND, Q2.E, Q3.E, J1.pin2, J1.pin6, C2.1, C3.0, T1.GND
  N1: J2.pin4, J4.pin2
  N2: J2.pin6, J4.pin5
  N3: J2.pin8, J5.pin2
  N4: J3.pin2, S1.COM
  N5: J3.pin5, J1.pin5
  5V: J4.pin1, U1.output_voltage, C2.0
  3.3V: J5.pin4, T1.+Vs
  N6: J5.pin5, T1.Vout
  N7: J6.pin2, R1.Pin_1
  N8: J6.pin5, J1.pin1
  N9: R1.Pin_0, Q2.B
  N10: R2.Pin_0, S1.L2
  N11: R2.Pin_1, Q3.B
  N12: Q2.C, J1.pin3
  N13: Q3.C, J1.pin7

notes:
  J1 PINOUT
  12V
  GND
  back door -
  back door +
  panic button -
  panic button +
  garage door -
  garage door +
  J2 PINOUT
  siren +
  siren -
  front door -
  front door +
  motion power +
  motion power -
  motion sensor -
  motion sensor +
  JEENODE IO
  DIO1 motion sensor
  AIO1 motion sensor power
  DIO2 front door
  AIO2 siren
  DIO3 back door
  AIO3 panic button
  DIO4 garage door
  AIO4 temperature sensor
  J3 (P2) PINS
  I
  A
  +
  G
  D
  P
  J6 (P1) PINS
  I
  A
  +
  G
  D
  P
  J5 (P4) PINS
  P
  D
  G
  +
  A
  I
  J4 (P3) PINS
  P
  D
  G
  +
  A
  I
  Security Node, Copyright (c) 2012 Ken Sharp, 1
